# Fritzing sketch flip_clock_(ds1307) (saved by Fritzing 0.8.5b)
breadboards: 1

parts:
  S1 = Pushbutton [package="[THT]"]
  S2 = Pushbutton [package="[THT]"]
  S3 = Pushbutton [package="[THT]"]
  Часть2 = Real Time Clock Module - DS1307 RTC Breakout Board
  R2 = Rotary Potentiometer (Small) [maximum_resistance=100kΩ package=THT]
  LED1 = LED - 5mm [color="Orange (620nm)" package="5 mm [THT]"]
  LED2 = LED - 5mm [color="Orange (620nm)" package="5 mm [THT]"]
  LED3 = LED - 5mm [color="Orange (620nm)" package="5 mm [THT]"]
  SPKR1 = Loudspeaker
  Часть3 = Arduino Nano (Rev3.0)
  R3 = Photocell (LDR) [package=THT]
  R4 = Resistor [tolerance=±5% resistance=220 package=THT]
  R5 = Resistor [tolerance=±5% resistance=4.7k package=THT]
  R6 = Resistor [tolerance=±5% resistance=4.7k package=THT]
  R7 = Resistor [tolerance=±5% resistance=4.7k package=THT]
  R8 = Resistor [tolerance=±5% resistance=100 package=THT]
  VCC1 = Battery block 9V
  R9 = Resistor [tolerance=±5% resistance=220 package=THT]
  R10 = Resistor [tolerance=±5% resistance=220 package=THT]
  R11 = Resistor [tolerance=±5% resistance=220 package=THT]
  R12 = Resistor [tolerance=±5% resistance=220 package=THT]
  R13 = Resistor [tolerance=±5% resistance=220 package=THT]

nets:
  N1: S1.Pin_1, S1.Pin_2, Часть3.D2, R7.Pin_0
  5V: S1.Pin_3, S1.Pin_4, S2.Pin_3, S2.Pin_4, S3.Pin_3, S3.Pin_4, Часть2.5V, R2.leg1, Часть3.5V, R3.pin_0
  N2: S2.Pin_1, S2.Pin_2, Часть3.D4, R6.Pin_0
  N3: S3.Pin_1, S3.Pin_2, Часть3.D7, R5.Pin_0
  GND: Часть2.GND, R2.leg2, LED1.cathode, LED2.cathode, LED3.cathode, Часть3.GND, R4.Pin_1, R5.Pin_1, R6.Pin_1, R7.Pin_1, VCC1.-, R10.Pin_1
  N4: Часть2.SCL, Часть3.A5
  N5: Часть2.SDA, Часть3.A4
  N6: R2.wiper, Часть3.A0
  N7: LED1.anode, R13.Pin_0
  N8: LED2.anode, R12.Pin_0
  N9: LED3.anode, R11.Pin_0
  N10: SPKR1.pin1, R8.Pin_0
  N11: SPKR1.pin2, Часть3.D9
  N12: Часть3.D3, R11.Pin_1
  N13: Часть3.D5, R12.Pin_1
  N14: Часть3.D6, R13.Pin_1
  N15: Часть3.D10, R8.Pin_1
  N16: Часть3.VIN, VCC1.+, R9.Pin_0
  N17: Часть3.A2, R9.Pin_1, R10.Pin_0
  N18: Часть3.A1, R3.pin_1, R4.Pin_0

notes:
  SELECT
  PLUS
  CANCEL
  alarm
  min
  hour
